// Logisim project test1.circ as structural Verilog: 1 circuit, main circuit main
module main (
  input  in_1,
  input  in_2,
  input  in_3,
  input  in_4,
  input  in_5,
  input  in_6,
  input  in_7,
  input  in_8,
  input  in_9,
  input  in_10,
  input  in_11,
  input  in_12,
  output out_13,
  output out_14,
  output out_15,
  output out_16,
  output out_17,
  output out_18,
  output out_19
);

  Controlled_Buffer controlled_buffer_1 (.in(in_6), .out(out_16));  // open: en
  nand nand_1 (out_13, in_1, in_2);
  and and_1 (out_14, in_3, in_4);
  not not_1 (out_15, in_5);
  nor nor_1 (out_17, in_7, in_8);
  xor xor_1 (out_18, in_9, in_10);
  xnor xnor_1 (out_19, in_11, in_12);
endmodule
