// Logisim project unit3-1.circ as structural Verilog: 1 circuit, main circuit main
module main (
  input  LSB,
  input  in_2,
  input  in_3,
  input  in_4,
  input  position_1,
  input  in_6,
  input  in_7,
  input  in_8,
  output out_9,
  output out_10,
  output out_11,
  output Result,
  output out_13,
  output out_14
);

  wire and_1_out, and_2_out, and_3_out, and_4_out, and_5_out, and_6_out, and_7_out, and_8_out, and_9_out,
       and_10_out, and_11_out, and_12_out, and_13_out, and_14_out, and_15_out, and_16_out, and_17_out,
       and_18_out, and_19_out, and_20_out, and_21_out, and_22_out, or_2_out;

  and and_1 (and_1_out, position_1, and_8_out);
  and and_2 (and_2_out, in_8, and_8_out);
  and and_3 (and_3_out, position_1, in_8);
  and and_4 (and_4_out, position_1, in_8, and_8_out);
  and and_5 (and_5_out, ~position_1, ~in_8, and_8_out);  // AND_Gate
  and and_6 (and_6_out, ~position_1, ~and_8_out, in_8);  // AND_Gate
  and and_7 (and_7_out, ~in_8, ~and_8_out, position_1);  // AND_Gate
  and and_8 (and_8_out, LSB, LSB, in_2);
  or or_1 (out_11, and_4_out, and_5_out, and_6_out, and_7_out);
  xor xor_1 (Result, in_2, LSB);
  or or_2 (or_2_out, and_1_out, and_2_out, and_3_out);
  and and_9 (and_9_out, in_3, or_2_out);
  and and_10 (and_10_out, in_6, or_2_out);
  and and_11 (and_11_out, in_3, in_6);
  and and_12 (and_12_out, in_3, in_6, or_2_out);
  and and_13 (and_13_out, ~in_3, ~in_6, or_2_out);  // AND_Gate
  and and_14 (and_14_out, ~in_3, ~or_2_out, in_6);  // AND_Gate
  and and_15 (and_15_out, ~in_6, ~or_2_out, in_3);  // AND_Gate
  or or_3 (out_13, and_9_out, and_10_out, and_11_out);
  or or_4 (out_10, and_12_out, and_13_out, and_14_out, and_15_out);
  and and_16 (and_16_out, in_4, out_13);
  and and_17 (and_17_out, in_7, out_13);
  and and_18 (and_18_out, in_4, in_7);
  and and_19 (and_19_out, in_4, in_7, out_13);
  and and_20 (and_20_out, ~in_4, ~in_7, out_13);  // AND_Gate
  and and_21 (and_21_out, ~in_4, ~out_13, in_7);  // AND_Gate
  and and_22 (and_22_out, ~in_7, ~out_13, in_4);  // AND_Gate
  or or_5 (out_14, and_16_out, and_17_out, and_18_out);
  or or_6 (out_9, and_19_out, and_20_out, and_21_out, and_22_out);

  // Notes on the sheet:
  //   postiion 0
  //   position 2
  //   position 3
endmodule
