// Logisim project unit3-2.circ as structural Verilog: 1 circuit, main circuit main
module main (
  input  B3,
  input  B2,
  input  B1,
  input  B0,
  input  in_5,
  input  in_6,
  input  in_7,
  input  in_8,
  input  in_9,
  input  A3,
  input  A2,
  input  A1,
  input  A0,
  input  in_14,
  output out_15,
  output out_16,
  output out_17,
  output out_18,
  output out_19,
  output out_20,
  output out_21,
  output out_22
);

  wire and_1_out, and_2_out, and_3_out, and_4_out, and_5_out, and_6_out, and_7_out, and_8_out, and_9_out,
       and_10_out, and_11_out, and_12_out, and_13_out, and_14_out, and_15_out, and_16_out, not_1_out,
       not_2_out, not_3_out, not_4_out, or_1_out, or_2_out, or_3_out, or_4_out, xor_1_out, xor_3_out,
       xor_4_out, xor_6_out, xor_8_out, xor_9_out, xor_10_out, xor_13_out, xor_14_out, xor_16_out,
       xor_17_out, xor_20_out;

  or or_1 (or_1_out, and_1_out, and_2_out);
  xor xor_1 (xor_1_out, and_3_out, and_4_out);
  and and_1 (and_1_out, A3, out_15);
  and and_2 (and_2_out, xor_3_out, or_2_out);
  xor xor_2 (out_19, or_2_out, xor_3_out);
  and and_3 (and_3_out, in_5, not_1_out);
  and and_4 (and_4_out, xor_4_out, xor_6_out);
  xor xor_3 (xor_3_out, A3, out_15);
  not not_1 (not_1_out, B3);
  xor xor_4 (xor_4_out, not_1_out, in_5);
  xor xor_5 (out_15, xor_6_out, xor_4_out);
  xor xor_6 (xor_6_out, and_5_out, and_6_out);
  or or_2 (or_2_out, and_7_out, and_8_out);
  xor xor_7 (out_20, or_3_out, xor_8_out);
  and and_5 (and_5_out, in_6, not_2_out);
  and and_6 (and_6_out, xor_9_out, xor_10_out);
  and and_7 (and_7_out, A2, out_16);
  and and_8 (and_8_out, xor_8_out, or_3_out);
  xor xor_8 (xor_8_out, A2, out_16);
  not not_2 (not_2_out, B2);
  xor xor_9 (xor_9_out, not_2_out, in_6);
  xor xor_10 (xor_10_out, and_9_out, and_10_out);
  xor xor_11 (out_16, xor_10_out, xor_9_out);
  or or_3 (or_3_out, and_11_out, and_12_out);
  and and_9 (and_9_out, in_7, not_3_out);
  and and_10 (and_10_out, xor_13_out, xor_14_out);
  and and_11 (and_11_out, A1, out_17);
  and and_12 (and_12_out, xor_16_out, or_4_out);
  xor xor_12 (out_21, or_4_out, xor_16_out);
  not not_3 (not_3_out, B1);
  xor xor_13 (xor_13_out, not_3_out, in_7);
  xor xor_14 (xor_14_out, and_13_out, and_14_out);
  xor xor_15 (out_17, xor_14_out, xor_13_out);
  xor xor_16 (xor_16_out, A1, out_17);
  and and_13 (and_13_out, in_8, not_4_out);
  and and_14 (and_14_out, xor_17_out, in_9);
  or or_4 (or_4_out, and_15_out, and_16_out);
  not not_4 (not_4_out, B0);
  xor xor_17 (xor_17_out, not_4_out, in_8);
  xor xor_18 (out_18, in_9, xor_17_out);
  and and_15 (and_15_out, A0, out_18);
  and and_16 (and_16_out, xor_20_out, in_14, in_14);
  xor xor_19 (out_22, in_14, xor_20_out);
  xor xor_20 (xor_20_out, A0, out_18);

  // Notes on the sheet:
  //   2's complement 
  //   output 
  //   Cin=0
endmodule
