// Logisim project unit1Discussion.circ as structural Verilog: 1 circuit, main circuit main
module main (
  input  in_1,
  input  in_2,
  input  in_3,
  input  in_4,
  output out_5,
  output out_6,
  output out_7,
  output out_8
);

  wire and_1_out, not_2_out;

  or or_1 (out_5, in_1, in_2);
  and and_1 (and_1_out, in_1, in_2);
  not not_1 (out_7, and_1_out);
  not not_2 (not_2_out, in_3);
  and and_2 (out_8, not_2_out, in_4, in_4);
  and and_3 (out_6, out_5, out_7);
endmodule
