// Logisim project unit3-3.circ as structural Verilog: 1 circuit, main circuit main
module main (
  input  [3:0] in_1,
  input  [3:0] in_2,
  input  [1:0] in_3,
  output [3:0] out_4,
  output [3:0] out_5,
  output [3:0] out_6,
  output [3:0] out_7,
  output [3:0] out_8
);

  Adder #(.width(4)) adder_1 (.a(in_1), .b(in_2), .out(out_4));  // open: cin, cout
  Subtractor #(.width(4)) subtractor_1 (.a(in_2), .b(in_1), .out(out_5));  // open: bin, bout
  assign out_7 = in_1 & in_2;  // AND_Gate and_1, 4 bits wide
  assign out_8 = in_1 | in_2;  // OR_Gate or_1, 4 bits wide
  Multiplexer #(.select(2), .width(4)) multiplexer_1 (
    .in0(out_4), .in1(out_5), .in2(out_7), .in3(out_8), .out(out_6), .sel(in_3));  // open: en
endmodule
